# Fritzing sketch Fritz (saved by Fritzing 0.9.2b)
circuit board: 8.46667cm x 5.64444cm

parts:
  D1 = Diode [package=diode-1n4001]
  Q1 = TRANSISTOR_NPN [package=to-92-ammo]
  R1 = Resistor [tolerance=±10% resistance=270 package=THT]
  Arduino_Uno = Arduino Uno (Rev3) - ICSP
  M1 = DC Motor

nets (from the breadboard view):
  N1: D1.A, Q1.E, M1.pin_1
  N2: D1.C, Arduino_Uno.5V, M1.pin_2
  N3: Q1.B, R1.Pin_0
  N4: Q1.C, Arduino_Uno.GND
  N5: R1.Pin_1, Arduino_Uno.D2
